// Digital circuit computer.dig as structural Verilog
module computer (
  input  clk
);

  wire MEM_OE, MEM_SEL, MEM_WE;
  wire [7:0] DBUS_I, DBUS_O;
  wire [14:0] MEM_ADDR;

  main main_1 (.C(clk), .DBUS(DBUS_I), .ABUS({MEM_SEL, MEM_ADDR}), .DBUS_O(DBUS_O), .MEM_OE(MEM_OE), .MEM_WE(MEM_WE));
  ROM rom_1 ();  // open: A, sel, D
endmodule
