// Digital circuit main.dig as structural Verilog
module main (
  input  clk
);

  wire A_RD_DB, A_WR_ALU, A_WR_DB, ACC_WR_DB, and_1_out, and_2_out, B_RD_DB, B_WR_ALU, B_WR_DB, C_RD_DB,
       C_WR_ALU, C_WR_DB, condition_unit_1_out, D_RD_DB, D_WR_ALU, D_WR_DB, demultiplexer_1_out_0,
       demultiplexer_1_out_1, IN_WR_DB, IR0_RD, IR1_RD, IR2_RD, MEM_OE, MEM_WE, microcode_1_upc_clr,
       microcode_1_upc_cond_clr, ooo, or_1_out, PC_H_WE, PC_INC, PC_L_WE, PC_ovf, PC_WR_AB, RS0_PAIR_WR_A,
       RS0_PAIR_WR_B, RS0_PAIR_WR_C, RS0_PAIR_WR_D, RS0_RD_DB, RS0_WR_DB, RS1_PAIR_WR_A, RS1_PAIR_WR_B,
       RS1_PAIR_WR_C, RS1_PAIR_WR_D, RS1_RD_DB, RS1_WR_DB, RS_PAIR_WR_AB, SP_DEC, SP_H_RD_DB, SP_H_WR_DB,
       SP_INC, SP_L_RD_DB, SP_L_WR_DB, SP_ovf, SP_WR_AB, STORE_ACC, STORE_FLAG, VVV_RD_DB, VVV_WR_DB,
       write_dbus_signals_1_sp_hi, write_dbus_signals_2_sp_hi;
  wire [1:0] AB_WR_DEV, ll;
  wire [2:0] DB_RD_DEV, DB_WR_DEV, PC_SRC, rs0, rs1, vvv;
  wire [3:0] alu_1_p1, FLAG_Data, microcode_1_upc;
  wire [7:0] A_q, ACC_Data, alu_1_p3, alu_1_p6, B_q, C_q, D_q, driver_3_out, driver_20_out, imm8,
       instruction_decoder_1_p4, instruction_decoder_1_p6, IR0_Data, multiplexer_1_out, rom_1_d, SP_hi, SP_lo;
  wire [11:0] microcode_1_addr;
  wire [15:0] add_1_s, bitextender_1_out, driver_1_out, driver_10_out, imm16, PC_Data;

  Decoder #(.Selector_Bits(3)) decoder_1 (
    .sel(vvv), .out_1(A_WR_ALU), .out_2(B_WR_ALU), .out_3(C_WR_ALU), .out_4(D_WR_ALU));  // open: out_0, out_5, out_6, out_7
  Decoder #(.Selector_Bits(3)) decoder_2 (
    .sel(rs0), .out_1(RS0_PAIR_WR_A), .out_2(RS0_PAIR_WR_B), .out_3(RS0_PAIR_WR_C), .out_4(RS0_PAIR_WR_D));  // open: out_0, out_5, out_6, out_7
  Decoder #(.Selector_Bits(3)) decoder_3 (
    .sel(DB_RD_DEV), .out_1(VVV_RD_DB), .out_2(RS0_RD_DB), .out_3(RS1_RD_DB), .out_5(SP_L_RD_DB),
    .out_6(SP_H_RD_DB));  // open: out_0, out_4, out_7
  condition_unit condition_unit_1 (.cond(vvv), .flags(FLAG_Data), .out(condition_unit_1_out));
  and and_1 (and_1_out, microcode_1_upc_cond_clr, condition_unit_1_out);
  BitExtender bitextender_1 (.in(imm8), .out(bitextender_1_out));
  Decoder #(.Selector_Bits(3)) decoder_4 (
    .sel(rs1), .out_1(RS1_PAIR_WR_A), .out_2(RS1_PAIR_WR_B), .out_3(RS1_PAIR_WR_C), .out_4(RS1_PAIR_WR_D));  // open: out_0, out_5, out_6, out_7
  or or_1 (or_1_out, SP_DEC, SP_INC);
  LED led_1 (.in(microcode_1_upc_clr));
  microcode microcode_1 (
    .d0(IR0_Data), .c(clk), .uPC_clr_2(and_1_out), .uPC_CLR(microcode_1_upc_clr), .PC_INC(PC_INC),
    .PCL_WE(PC_L_WE), .PCH_WE(PC_H_WE), .IR0_RD(IR0_RD), .IR1_RD(IR1_RD), .IR2_RD(IR2_RD), .SP_INC(SP_INC),
    .SP_DEC(SP_DEC), .DB_RD_DEV(DB_RD_DEV), .DB_WR_DEV(DB_WR_DEV), .AB_WR_DEV(AB_WR_DEV),
    .STORE_FLAG(STORE_FLAG), .STORE_ACC(STORE_ACC), .MEM_WE(MEM_WE), .MEM_OE(MEM_OE), .PC_SRC(PC_SRC),
    .uPC_Cond_CLR(microcode_1_upc_cond_clr), .uPC(microcode_1_upc), .ADDR(microcode_1_addr));
  Add #(.Bits(16)) add_1 (.a(PC_Data), .b(bitextender_1_out), .c_i(1'b0), .s(add_1_s));  // open: c_o
  Multiplexer #(.Selector_Bits(3), .Bits(8)) multiplexer_1 (
    .sel(PC_SRC), .in_0(driver_3_out), .in_1(add_1_s[7:0]), .in_2(add_1_s[15:8]), .in_3(imm16[7:0]),
    .in_4(imm16[15:8]), .in_5({8{1'b0}}), .in_6({8{1'b0}}), .in_7({8{1'b0}}), .out(multiplexer_1_out));
  write_dbus_signals write_dbus_signals_1 (
    .vvv(vvv), .rs0(rs0), .rs1(rs1), .R_vvv(VVV_RD_DB), .R_rs0(RS0_RD_DB), .R_rs1(RS1_RD_DB), .A(A_RD_DB),
    .B(B_RD_DB), .C(C_RD_DB), .D(D_RD_DB), .SP_Hi(write_dbus_signals_1_sp_hi));  // open: SP_Lo
  write_dbus_signals write_dbus_signals_2 (
    .vvv(vvv), .rs0(rs0), .rs1(rs1), .R_vvv(VVV_WR_DB), .R_rs0(RS0_WR_DB), .R_rs1(RS1_WR_DB), .A(A_WR_DB),
    .B(B_WR_DB), .C(C_WR_DB), .D(D_WR_DB), .SP_Hi(write_dbus_signals_2_sp_hi));  // open: SP_Lo
  Decoder #(.Selector_Bits(3)) decoder_5 (
    .sel(DB_WR_DEV), .out_1(VVV_WR_DB), .out_2(RS0_WR_DB), .out_3(RS1_WR_DB), .out_4(ACC_WR_DB),
    .out_5(SP_L_WR_DB), .out_6(SP_H_WR_DB), .out_7(IN_WR_DB));  // open: out_0
  _16_bit_presettable_counter PC (
    .en(PC_INC), .c(clk), .dir(1'b0), .lo_in(multiplexer_1_out), .lo_ld(PC_L_WE), .hi_in(multiplexer_1_out),
    .hi_ld(PC_H_WE), .clr(1'b0), .ovf(PC_ovf), .lo(PC_Data[7:0]), .hi(PC_Data[15:8]));
  LED led_2 (.in(PC_ovf));
  _16_bit_presettable_counter SP (
    .en(or_1_out), .c(clk), .dir(SP_DEC), .lo_in(driver_3_out), .lo_ld(SP_L_RD_DB), .hi_in(driver_3_out),
    .hi_ld(SP_H_RD_DB), .clr(1'b0), .ovf(SP_ovf), .lo(SP_lo), .hi(SP_hi));
  // Probe on microcode_1_addr
  assign driver_1_out = PC_WR_AB ? PC_Data : 16'bz;  // Driver driver_1
  LED led_3 (.in(SP_ovf));
  assign driver_1_out = SP_WR_AB ? {SP_hi, SP_lo} : 16'bz;  // Driver driver_2
  assign driver_3_out = SP_L_WR_DB ? SP_lo : 8'bz;  // Driver driver_3
  assign driver_3_out = SP_H_WR_DB ? SP_hi : 8'bz;  // Driver driver_4
  LED led_4 (.in(write_dbus_signals_1_sp_hi));
  LED led_5 (.in(write_dbus_signals_2_sp_hi));
  // Probe on microcode_1_upc
  Demultiplexer demultiplexer_1 (
    .sel(driver_1_out[0]), .in(MEM_OE), .out_0(demultiplexer_1_out_0), .out_1(demultiplexer_1_out_1));
  Decoder #(.Selector_Bits(2)) decoder_6 (
    .sel(AB_WR_DEV), .out_1(PC_WR_AB), .out_2(SP_WR_AB), .out_3(RS_PAIR_WR_AB));  // open: out_0
  ROM #(.AddrBits(15), .Bits(8)) rom_1 (.A(driver_1_out[15:1]), .sel(demultiplexer_1_out_0), .D(rom_1_d));
  assign driver_1_out = RS_PAIR_WR_AB ? driver_10_out : 16'bz;  // Driver driver_5
  assign driver_3_out = IN_WR_DB ? rom_1_d : 8'bz;  // Driver driver_6
  assign driver_3_out = ACC_WR_DB ? ACC_Data : 8'bz;  // Driver driver_7
  RAMDualPort #(.AddrBits(15), .Bits(8)) ramdualport_1 (
    .A(driver_1_out[15:1]), .Din(driver_3_out), .str(MEM_WE), .C(clk), .ld(demultiplexer_1_out_1), .D(rom_1_d));
  Register #(.Bits(8)) A (.D(driver_3_out), .C(clk), .en(A_RD_DB), .Q(A_q));
  assign driver_3_out = A_WR_DB ? A_q : 8'bz;  // Driver driver_8
  assign driver_10_out[15:8] = RS0_PAIR_WR_A ? A_q : 8'bz;  // Driver driver_9
  assign driver_10_out[7:0] = RS1_PAIR_WR_A ? A_q : 8'bz;  // Driver driver_10
  Register #(.Bits(8)) B (.D(driver_3_out), .C(clk), .en(B_RD_DB), .Q(B_q));
  assign driver_3_out = B_WR_DB ? B_q : 8'bz;  // Driver driver_11
  assign driver_10_out[15:8] = RS0_PAIR_WR_B ? B_q : 8'bz;  // Driver driver_12
  assign driver_10_out[7:0] = RS1_PAIR_WR_B ? B_q : 8'bz;  // Driver driver_13
  Register #(.Bits(8)) C (.D(driver_3_out), .C(clk), .en(C_RD_DB), .Q(C_q));
  assign driver_3_out = C_WR_DB ? C_q : 8'bz;  // Driver driver_14
  assign driver_10_out[15:8] = RS0_PAIR_WR_C ? C_q : 8'bz;  // Driver driver_15
  assign driver_10_out[7:0] = RS1_PAIR_WR_C ? C_q : 8'bz;  // Driver driver_16
  Register #(.Bits(8)) D (.D(driver_3_out), .C(clk), .en(D_RD_DB), .Q(D_q));
  assign driver_3_out = D_WR_DB ? D_q : 8'bz;  // Driver driver_17
  assign driver_10_out[15:8] = RS0_PAIR_WR_D ? D_q : 8'bz;  // Driver driver_18
  assign driver_10_out[7:0] = RS1_PAIR_WR_D ? D_q : 8'bz;  // Driver driver_19
  Register #(.Bits(8)) ACC (.D(alu_1_p3), .C(clk), .en(STORE_ACC), .Q(ACC_Data));
  // Probe on A_q
  assign driver_20_out = A_WR_ALU ? A_q : 8'bz;  // Driver driver_20
  assign driver_20_out = B_WR_ALU ? B_q : 8'bz;  // Driver driver_21
  assign driver_20_out = C_WR_ALU ? C_q : 8'bz;  // Driver driver_22
  assign driver_20_out = D_WR_ALU ? D_q : 8'bz;  // Driver driver_23
  // alu alu_1: pin names not known; wires that end beside it: alu_1_p1, driver_20_out, alu_1_p3, FLAG_Data, ooo, alu_1_p6
  Multiplexer #(.Bits(8)) multiplexer_2 (.sel(and_2_out), .in_0(ACC_Data), .in_1(imm8), .out(alu_1_p6));
  Register #(.Bits(8)) IR0 (.D(driver_3_out), .C(clk), .en(IR0_RD), .Q(IR0_Data));
  and and_2 (and_2_out, ll[0], ~ll[1]);  // And
  // Probe on IR0_Data
  Register #(.Bits(4)) FLAG (.D(alu_1_p1), .C(clk), .en(STORE_FLAG), .Q(FLAG_Data));
  // instruction_decoder instruction_decoder_1: pin names not known; wires that end beside it: ll, IR0_Data, ooo, instruction_decoder_1_p4, vvv, instruction_decoder_1_p6, imm8, rs0, rs1, imm16
  Register #(.Bits(8)) IR1 (.D(driver_3_out), .C(clk), .en(IR1_RD), .Q(instruction_decoder_1_p4));
  Register #(.Bits(8)) IR2 (.D(driver_3_out), .C(clk), .en(IR2_RD), .Q(instruction_decoder_1_p6));

  // Notes on the sheet:
  //   RS Pair Decoder
  //   DBUS Read Decoder
  //   ALU Decoder
  //   Branch Logic
  //   Program Counter
  //   Stack Pointer
  //   DBUS Write Decoder
  //   Microcode and Clock
  //   DBUS Signals
  //   ABUS Decoder
  //   DBUS
  //   ABUS
  //   contents of rom_1 (hex, n*v repeats v):
  //   1,9
  //   Registers
  //   ALU and FLAG
  //   IRs and Decoder
endmodule
