// Digital circuit microcode.dig as structural Verilog
module microcode (
  input  [7:0] d0,
  input  c,
  input  uPC_clr_2,
  output uPC_CLR,
  output PC_INC,
  output PCL_WE,
  output PCH_WE,
  output IR0_RD,
  output IR1_RD,
  output IR2_RD,
  output SP_INC,
  output SP_DEC,
  output [2:0] DB_RD_DEV,
  output [2:0] DB_WR_DEV,
  output [1:0] AB_WR_DEV,
  output STORE_FLAG,
  output STORE_ACC,
  output MEM_WE,
  output MEM_OE,
  output [2:0] PC_SRC,
  output uPC_Cond_CLR,
  output [3:0] uPC,
  output [11:0] ADDR
);

  wire or_1_out;
  wire [7:1] _3_d;

  ROM #(.AddrBits(12), .Bits(8)) _3 (.A({d0, ADDR[3:0]}), .sel(1'b1), .D({_3_d, MEM_OE}));
  or or_1 (or_1_out, uPC_clr_2, uPC_CLR);
  ROM #(.AddrBits(12), .Bits(8)) _2 (
    .A({d0, ADDR[3:0]}), .sel(1'b1), .D({MEM_WE, STORE_ACC, STORE_FLAG, DB_WR_DEV, DB_RD_DEV[2:1]}));
  Counter #(.Bits(4)) u_uPC (.en(1'b1), .C(c), .clr(or_1_out), .out(ADDR[3:0]));  // open: ovf
  ROM #(.AddrBits(12), .Bits(8)) _1 (
    .A({d0, ADDR[3:0]}), .sel(1'b1), .D({DB_RD_DEV[0], AB_WR_DEV, SP_DEC, SP_INC, IR2_RD, IR1_RD, IR0_RD}));
  ROM #(.AddrBits(12), .Bits(8)) _0 (
    .A({d0, ADDR[3:0]}), .sel(1'b1), .D({PC_SRC, PCH_WE, PCL_WE, PC_INC, uPC_Cond_CLR, uPC_CLR}));

  assign ADDR[11:4] = d0;
  assign uPC = ADDR[3:0];

  // Notes on the sheet:
  //   contents of _3 (hex, n*v repeats v):
  //   1,15*0,1,15*0,1,15*0,1,15*0,1,15*0,1,15*0,1,15*0,1,15*0,1,15*0
  //   ,1,15*0,1,15*0,1,15*0,1,15*0,1,15*0,1,15*0,1
  //   contents of _2 (hex, n*v repeats v):
  //   1c,10,14*0,1c,10,14*0,1c,10,14*0,1c,10,14*0,1c,10,14*0,1c,10,14*0
  //   ,1c,10,14*0,1c,10,14*0,1c,40,14*0,1c,40,14*0,1c,40,14*0,1c,40
  //   ,14*0,1c,40,14*0,1c,40,14*0,1c,40,14*0,1c,40
  //   contents of _1 (hex, n*v repeats v):
  //   21,80,14*0,21,80,14*0,21,80,14*0,21,80,14*0,21,80,14*0,21,80,14*0
  //   ,21,80,14*0,21,80,14*0,21,15*0,21,15*0,21,15*0,21,15*0,21,15*0
  //   ,21,15*0,21,15*0,21
  //   contents of _0 (hex, n*v repeats v):
  //   4,1,14*0,4,1,14*0,4,1,14*0,4,1,14*0,4,1,14*0,4,1,14*0,4,1,14*0
  //   ,4,1,14*0,4,1,14*0,4,1,14*0,4,1,14*0,4,1,14*0,4,1,14*0,4,1,14*0
  //   ,4,1,14*0,4,1
endmodule
